// Digital circuit 10x17_RAM.dig as structural Verilog
module _10x17_RAM (
  input  [16:0] WRD__16_0,
  input  [3:0] WR__3_0,
  input  CLK,
  input  WE,
  input  [3:0] RA1__3_0,
  input  [3:0] RA2__3_0,
  output [16:0] RD1__16_0,
  output [16:0] RD2__16_0
);

  wire decoder_1_out_10, decoder_2_out_10, decoder_3_out_10, R1_0, R1_1, R1_2, R1_3, R1_4, R1_5, R1_6, R1_7,
       R1_8, R1_9, R2_0, R2_1, R2_2, R2_3, R2_4, R2_5, R2_6, R2_7, R2_8, R2_9, W0, W1, W2, W3, W4, W5, W6,
       W7, W8, W9, WS0, WS1, WS2, WS3, WS4, WS5, WS6, WS7, WS8, WS9;
  wire [16:0] or_1_out, or_2_out, or_3_out, or_4_out, RD1_0, RD1_1, RD1_2, RD1_3, RD1_4, RD1_5, RD1_6, RD1_7,
       RD1_8, RD1_9, RD2_0, RD2_1, RD2_2, RD2_3, RD2_4, RD2_5, RD2_6, RD2_7, RD2_8, RD2_9;

  Decoder #(.Selector_Bits(4)) decoder_1 (
    .sel(WR__3_0), .out_0(W0), .out_1(W1), .out_2(W2), .out_3(W3), .out_4(W4), .out_5(W5), .out_6(W6),
    .out_7(W7), .out_8(W8), .out_9(W9), .out_10(decoder_1_out_10), .out_11(decoder_1_out_10),
    .out_12(decoder_1_out_10), .out_13(decoder_1_out_10), .out_14(decoder_1_out_10), .out_15(decoder_1_out_10));
  Decoder #(.Selector_Bits(4)) decoder_2 (
    .sel(RA1__3_0), .out_0(R1_0), .out_1(R1_1), .out_2(R1_2), .out_3(R1_3), .out_4(R1_4), .out_5(R1_5),
    .out_6(R1_6), .out_7(R1_7), .out_8(R1_8), .out_9(R1_9), .out_10(decoder_2_out_10),
    .out_11(decoder_2_out_10), .out_12(decoder_2_out_10), .out_13(decoder_2_out_10),
    .out_14(decoder_2_out_10), .out_15(decoder_2_out_10));
  and and_1 (WS9, W9, WE);
  and and_2 (WS7, W7, WE);
  and and_3 (WS5, W5, WE);
  and and_4 (WS3, W3, WE);
  and and_5 (WS1, W1, WE);
  Decoder #(.Selector_Bits(4)) decoder_3 (
    .sel(RA2__3_0), .out_0(R2_0), .out_1(R2_1), .out_2(R2_2), .out_3(R2_3), .out_4(R2_4), .out_5(R2_5),
    .out_6(R2_6), .out_7(R2_7), .out_8(R2_8), .out_9(R2_9), .out_10(decoder_3_out_10),
    .out_11(decoder_3_out_10), .out_12(decoder_3_out_10), .out_13(decoder_3_out_10),
    .out_14(decoder_3_out_10), .out_15(decoder_3_out_10));
  and and_6 (WS8, W8, WE);
  and and_7 (WS6, W6, WE);
  and and_8 (WS4, W4, WE);
  and and_9 (WS2, W2, WE);
  and and_10 (WS0, W0, WE);
  _1x17_RAM _1x17_ram_1 (
    .RS1(R1_9), .RS2(R2_9), .WS(WS9), .WD_16_0(WRD__16_0), .CLK(CLK), .RD1_16_0(RD1_9), .RD2_16_0(RD2_9));
  _1x17_RAM _1x17_ram_2 (
    .RS1(R1_7), .RS2(R2_7), .WS(WS7), .WD_16_0(WRD__16_0), .CLK(CLK), .RD1_16_0(RD1_7), .RD2_16_0(RD2_7));
  _1x17_RAM _1x17_ram_3 (
    .RS1(R1_5), .RS2(R2_5), .WS(WS5), .WD_16_0(WRD__16_0), .CLK(CLK), .RD1_16_0(RD1_5), .RD2_16_0(RD2_5));
  _1x17_RAM _1x17_ram_4 (
    .RS1(R1_3), .RS2(R2_3), .WS(WS3), .WD_16_0(WRD__16_0), .CLK(CLK), .RD1_16_0(RD1_3), .RD2_16_0(RD2_3));
  _1x17_RAM _1x17_ram_5 (
    .RS1(R1_1), .RS2(R2_1), .WS(WS1), .WD_16_0(WRD__16_0), .CLK(CLK), .RD1_16_0(RD1_1), .RD2_16_0(RD2_1));
  _1x17_RAM _1x17_ram_6 (
    .RS1(R1_8), .RS2(R2_8), .WS(WS8), .WD_16_0(WRD__16_0), .CLK(CLK), .RD1_16_0(RD1_8), .RD2_16_0(RD2_8));
  _1x17_RAM _1x17_ram_7 (
    .RS1(R1_6), .RS2(R2_6), .WS(WS6), .WD_16_0(WRD__16_0), .CLK(CLK), .RD1_16_0(RD1_6), .RD2_16_0(RD2_6));
  _1x17_RAM _1x17_ram_8 (
    .RS1(R1_4), .RS2(R2_4), .WS(WS4), .WD_16_0(WRD__16_0), .CLK(CLK), .RD1_16_0(RD1_4), .RD2_16_0(RD2_4));
  _1x17_RAM _1x17_ram_9 (
    .RS1(R1_2), .RS2(R2_2), .WS(WS2), .WD_16_0(WRD__16_0), .CLK(CLK), .RD1_16_0(RD1_2), .RD2_16_0(RD2_2));
  _1x17_RAM _1x17_ram_10 (
    .RS1(R1_0), .RS2(R2_0), .WS(WS0), .WD_16_0(WRD__16_0), .CLK(CLK), .RD1_16_0(RD1_0), .RD2_16_0(RD2_0));
  assign or_1_out = RD1_9 | RD1_8 | RD1_7 | RD1_6 | RD1_5;  // Or or_1, 17 bits wide
  assign or_2_out = RD1_4 | RD1_3 | RD1_2 | RD1_1 | RD1_0;  // Or or_2, 17 bits wide
  assign or_3_out = RD2_9 | RD2_8 | RD2_7 | RD2_6 | RD2_5;  // Or or_3, 17 bits wide
  assign or_4_out = RD2_4 | RD2_3 | RD2_2 | RD2_1 | RD2_0;  // Or or_4, 17 bits wide
  assign RD1__16_0 = or_1_out | or_2_out;  // Or or_5, 17 bits wide
  assign RD2__16_0 = or_3_out | or_4_out;  // Or or_6, 17 bits wide
  // also tied to GND on the sheet: {decoder_3_out_10, decoder_2_out_10, decoder_1_out_10}

  // Other names for the same wires on the sheet: WRD[16:0] = WRD__16_0
endmodule
