// Digital circuit 4bit_PC.dig as structural Verilog
module _4bit_PC (
  input  [3:0] I__3_0,
  input  CLK,
  output [3:0] O__3_0
);

  _1bit_Reg _1bit_reg_1 (.Din(I__3_0[0]), .Sel(1'b1), .CLK(CLK), .Dout(O__3_0[0]));
  _1bit_Reg _1bit_reg_2 (.Din(I__3_0[1]), .Sel(1'b1), .CLK(CLK), .Dout(O__3_0[1]));
  _1bit_Reg _1bit_reg_3 (.Din(I__3_0[2]), .Sel(1'b1), .CLK(CLK), .Dout(O__3_0[2]));
  _1bit_Reg _1bit_reg_4 (.Din(I__3_0[3]), .Sel(1'b1), .CLK(CLK), .Dout(O__3_0[3]));

  // Other names for the same wires on the sheet: A0 = I__3_0[0]; A1 = I__3_0[1]; A2 = I__3_0[2]; A3 = I__3_0[3]
endmodule
