// Digital circuit 4bit_PC_Adder.dig as structural Verilog
module _4bit_PC_Adder (
  input  [3:0] I__3_0,
  output [3:0] O__3_0
);

  wire and_1_out;
  wire [3:0] temp;

  Add #(.Bits(4)) add_1 (.a(I__3_0), .b(4'b0001), .c_i(1'b0), .s(temp));  // open: c_o
  and and_1 (and_1_out, temp[1], temp[3]);
  Multiplexer #(.Bits(4)) multiplexer_1 (.sel(and_1_out), .in_0(temp), .in_1(4'b0000), .out(O__3_0));

  // Other names for the same wires on the sheet: I[3:0] = I__3_0; O[3:0] = O__3_0
endmodule
