// Digital circuit 5bit_ALU.dig as structural Verilog
module _5bit_ALU (
  input  [4:0] A_4_0,
  input  [4:0] B_4_0,
  input  [1:0] OP_1_0,
  output [4:0] R_4_0,
  output CF
);

  wire [4:0] _5bit_adder_1_r_4_0, _5bit_and_1_r_4_0, _5bit_rol_1_r_4_0;

  _5bit_ADDER _5bit_adder_1 (.A_4_0(A_4_0), .B_4_0(B_4_0), .R_4_0(_5bit_adder_1_r_4_0), .Cout(CF));
  _5bit_ROL _5bit_rol_1 (.A_4_0(A_4_0), .B_4_0(B_4_0), .R_4_0(_5bit_rol_1_r_4_0));
  _5bit_AND _5bit_and_1 (.A_4_0(A_4_0), .B_4_0(B_4_0), .R_4_0(_5bit_and_1_r_4_0));
  Multiplexer #(.Selector_Bits(2), .Bits(5)) multiplexer_1 (
    .sel(OP_1_0), .in_0(_5bit_adder_1_r_4_0), .in_1(_5bit_rol_1_r_4_0), .in_2(_5bit_and_1_r_4_0),
    .in_3({5{1'b0}}), .out(R_4_0));
endmodule
