// Digital circuit 5bit_CPU.dig as structural Verilog
module _5bit_CPU (
  input  [3:0] RA2__3_0,
  input  [3:0] WR__3_0,
  input  [16:0] WRD__16_0,
  input  WE,
  input  CLK,
  input  PC_EN,
  output [16:0] RD2__16_0,
  output [2:0] R2__2_0,
  output [2:0] R1__2_0,
  output [2:0] WR__2_0,
  output [4:0] A__4_0,
  output [4:0] B__4_0,
  output [4:0] R__4_0
);

  wire CF, CPU_CLK, Imm_Sel, JMP_Sel, REG_EN;
  wire [1:0] Imm_val, Op;
  wire [3:0] _4bit_pc_1_o__3_0, _4bit_pc_adder_1_o__3_0, _10x17_ram_1_rd1__16_0, multiplexer_1_out;
  wire [4:0] _5bit_reg_set_1_b_4_0, XX;

  Multiplexer #(.Bits(4)) multiplexer_1 (
    .sel(JMP_Sel), .in_0(_4bit_pc_adder_1_o__3_0), .in_1({R1__2_0, R2__2_0[2]}), .out(multiplexer_1_out));
  _4bit_PC_Adder _4bit_pc_adder_1 (.O__3_0(_4bit_pc_adder_1_o__3_0), .I__3_0(_4bit_pc_1_o__3_0));
  _4bit_PC _4bit_pc_1 (.I__3_0(multiplexer_1_out), .CLK(CPU_CLK), .O__3_0(_4bit_pc_1_o__3_0));
  and and_1 (CPU_CLK, PC_EN, CLK);
  _10x17_RAM _10x17_ram_1 (
    .RA1__3_0(_4bit_pc_1_o__3_0), .RA2__3_0(RA2__3_0), .WR__3_0(WR__3_0), .WRD__16_0(WRD__16_0), .WE(WE),
    .CLK(CLK), .RD1__16_0({_10x17_ram_1_rd1__16_0, R1__2_0, R2__2_0, Imm_val, XX}), .RD2__16_0(RD2__16_0));
  _5bit_CU _5bit_cu_1 (
    .Op_1_0(Op), .REG_EN(REG_EN), .Imm_Sel(Imm_Sel), .Jmp_Sel(JMP_Sel), .Opcode_3_0(_10x17_ram_1_rd1__16_0),
    .CF(CF));
  _5bit_Reg_Set _5bit_reg_set_1 (
    .RA_2_0(R1__2_0), .RB_2_0(R2__2_0), .WR_2_0(R1__2_0), .CLK(CPU_CLK), .WE(REG_EN), .WRD_4_0(R__4_0),
    .A_4_0(A__4_0), .B_4_0(_5bit_reg_set_1_b_4_0));
  _5bit_ALU _5bit_alu_1 (.A_4_0(A__4_0), .B_4_0(B__4_0), .OP_1_0(Op), .R_4_0(R__4_0), .CF(CF));
  Multiplexer #(.Bits(5)) multiplexer_2 (
    .sel(Imm_Sel), .in_0(_5bit_reg_set_1_b_4_0), .in_1({R2__2_0, Imm_val}), .out(B__4_0));

  assign WR__2_0 = R1__2_0;

  // Other names for the same wires on the sheet: XX[6:5] = Imm_val; Imm_val[4:2] = R2__2_0; R2[2:0] = R2__2_0;
  //   JMP_ADDR[3:0] = {R1__2_0, R2__2_0[2]}; R1[2:0] = R1__2_0; A[4:0] = A__4_0; B[4:0] = B__4_0;
  //   RD2[16:0] = RD2__16_0

  // Notes on the sheet:
  //   Register Mode (Type of Op=00) = 2bit(Type of Op) + 2bit (Op) + 3bit (Reg1) + 3bit (Reg2) + 7bit (Don't care) 
  //   Immediate Mode (Type of Op=01) = 2bit(Type of Op) + 2bit (Op) + 3bit (Reg1) + 5bit (Imm Val) + 5bit (Don't care)
  //   Jump Mode (Type of Op=10) = 2bit(Type of Op) + 2bit (Op) + 4bit (Address) + 9bit (Don't care)
  //   Add (Op = 00), ROL (Op = 01), AND (Op = 10)
  //   JMP (Op = 00), JC (Op = 01)
endmodule
